# Fritzing sketch wearable (saved by Fritzing 0.9.6b)
breadboards: 1

parts:
  microSD1 = MicroSD Card Module
  S1 = Momentary Switch [package=ksa_sealed_tac_switch]
  Part3 = Breakout Board for Electret Microphone
  R1 = Resistor [tolerance=±5% resistance=220 package="0805 [SMD]"]
  Mod1 = Heltec WiFi LoRa 32 V2 [part_number=HTIT-WB32LA]

nets:
  GND: microSD1.GND, Part3.GND, R1.Pin_0, Mod1.GND
  VCC: microSD1.VCC, S1.4, Part3.Vdd, Mod1.CLK, Mod1.V5
  N1: microSD1.MISO, Mod1.G19
  N2: microSD1.MOSI, Mod1.G23
  N3: microSD1.SCK, Mod1.G18
  N4: microSD1.CS, Mod1.G5
  N5: S1.1, Mod1.G2
  N6: S1.2, R1.Pin_1
  N7: Part3.Out, Mod1.G35

custom parts:
  Breakout Board for Electret Microphone: Description: Ready to add audio to your next project? This small breakout board couples a small electret microphone with a 100x opamp to amplify the sounds of voice, door knocks, etc loud enough to be picked up by a microcontroller's Analog to Digital converter. Unit comes fully assembled as shown. Works from 2.7V up to 5.5V. Documents: Schematic Example PIC ADC Code OPA344 Datasheet Example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
  Heltec WiFi LoRa 32 V2: The Heltec WiFi LoRa 32 is an IoT development board designed and produced by Heltec Automation and based on the Espressif ESP32 and Semtech SX127x modules. The board includes WiFi, Bluetooth and LoRa functions, as well as a 0.96″ OLED display and a lithium battery management system. Links: Heltec WiFi LoRa 32 product page Github
